# Fritzing sketch 3D Scanner_Schematic (saved by Fritzing 0.9.3b)
breadboards: 1

parts:
  M1 = Stepper Motor - Bipolar  # not connected
  Part1 = Arduino Uno (Rev3) - ICSP
  M2 = Stepper Motor - Bipolar  # not connected
  DRV_1 = DRV 8825 Stepper Motor Carrier, High Current [part_number="DRV 8825"]  # not connected
  DRV_2 = DRV 8825 Stepper Motor Carrier, High Current [part_number="DRV 8825"]  # not connected
  Power_plug1 = Power plug  # not connected
  Part2 = Adafruit VL530X Time of Flight Distance Sensor [part_number="Adafruit #3317"]
  U1 = LCD-16X2 [package=lcd-16x2]
  microSD1 = MicroSD Card Module
  S1 = Round Pushbutton
  JL012-13-5_1 = JL012-13-5.2 Lever (Limit) Switch SPDT + NO + NC [part_number=JL012-13-5.2]

nets:
  N1: Part1.A0, S1.leg1
  N2: Part1.A1, JL012-13-5_1.NC
  N3: Part1.ICSP_MOSI, Part1.D11_PWM/MOSI, microSD1.MOSI
  GND: Part1.GND, U1.VSS, U1.K
  N4: Part1.D10_PWM/SS, microSD1.CS
  N5: Part1.D12/MISO, microSD1.MISO
  N6: Part1.D13/SCK, microSD1.SCK
  N7: Part1.A4/SDA, Part2.SDA
  N8: Part1.A5/SCL, Part2.SCL
  5V: Part1.5V, U1.VDD, U1.A

custom parts:
  Adafruit VL530X Time of Flight Distance Sensor: The VL53L0X is a Time of Flight distance sensor like no other you've used! The sensor contains a very tiny invisible laser source, and a matching sensor. The VL53L0X can detect the "time of flight", or how long the light has taken to bounce back to the sensor. Since it uses a very narrow light source, it is good for determining distance of only the surface directly in front of it. Unlike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
  JL012-13-5.2 Lever (Limit) Switch SPDT + NO + NC: Micro Switch; Model No.: JL012-13.5-2; Actuator Action: Momentary; Actuator Type: Hinge Lever; Contact Configuration: 1NO, 1NC (SPDT) Temperature -25~65℃；Relative humidity: below 85%; Rate Voltage: 125V AC; Rated Current: 1A.
